# Fritzing sketch mycircuit (saved by Fritzing 0.9.3b)

parts:
  Part1 = Maker Uno (Arduino Uno Compatible)
  Part2 = Bluetooth HC-05 Macho
  Part3 = Black Joystick KY-023

nets:
  N1: Part1.A0, Part3.VRx
  N2: Part1.A1, Part3.VRy
  GND: Part1.GND, Part2.GND, Part3.GND
  5V: Part1.5V, Part2.VCC, Part3.+5V

custom parts:
  Maker Uno (Arduino Uno Compatible): Maker Uno, an Arduino UNO compatible board designed and developed specially for students to learn coding and microcontroller. We named it Maker UNO to encourage everyone to be a maker by getting started with this amazing board. Oh! BTW, it is PURPLE color.
  Black Joystick KY-023: Description: The joystick is a combination of 2 analoog potentiometer and a digital switch. Arduino GND --> Module pin - Arduino +5V --> Module pin +5V Arduino Analoog 0 --> Module VRx Arduino Analoog 1 --> Module VRy Arduino Digital --> Module SW Dimensions: 1" x 1.25"
